# Fritzing sketch Circuit v7 (saved by Fritzing 0.9.2b)
circuit board: 6cm x 11.5cm
breadboards: 1

parts:
  Arduino_Mini = Arduino Pro Mini v13
  FTDI = FTDI Basic Programmer
  Tmp/Hmd = female pin header, 3 pins [form="♀ (female)"]
  LDR = Photocell (LDR) [package=THT]
  10_K = Resistor [tolerance=±5% resistance=220 package=THT]
  Pantalla_LCD = Nokia5110LCDModule
  Temp/Hume2 = female pin header, 2 pins [form="♀ (female)"]
  Temp/Hume5 = female pin header, 8 pins [form="♀ (female)"]
  Bateria = female pin header, 2 pins [form="♀ (female)"]
  Celda_1 = female pin header, 2 pins [form="♀ (female)"]
  Celda_2 = female pin header, 2 pins [form="♀ (female)"]
  D1 = Rectifier Diode [part_number=1N4001 package="300 mil [THT]"]
  100uF = Electrolytic Capacitor [capacitance=1µF package="100 mil [THT, electrolytic]"]
  LED1 = LED - 5mm [color="Red (633nm)" package="5 mm [THT]"]
  R1 = Resistor [tolerance=±5% resistance=220 package=THT]
  XBee = female pin header, 6 pins [form="♀ (female)"]
  LUZ = female pin header, 5 pins [form="♀ (female)"]
  Moisture = female pin header, 3 pins [form="♀ (female)"]
  R2 = Resistor [tolerance=±5% resistance=220 package=THT]
  R3 = Resistor [tolerance=±5% resistance=220 package=THT]
  PH = female pin header, 6 pins [form="♀ (female)"]
  Celda_3 = female pin header, 2 pins [form="♀ (female)"]  # not connected
  Celda_4 = female pin header, 2 pins [form="♀ (female)"]  # not connected
  Tmp/Hmd1 = female pin header, 2 pins [form="♀ (female)"]  # not connected
  Tmp/Hmd2 = female pin header, 2 pins [form="♀ (female)"]  # not connected

nets:
  N1: Arduino_Mini.DTR, FTDI.DTR, R3.Pin_1
  N2: Arduino_Mini.D0/TX, FTDI.RXI
  N3: Arduino_Mini.D1/RX, FTDI.TXO
  VCC: Arduino_Mini.VCC, FTDI.POWER, Tmp/Hmd.pin2, LDR.pin_0, Pantalla_LCD.Vcc, Temp/Hume2.pin1, Temp/Hume2.pin2, Temp/Hume5.pin8, XBee.pin4, LUZ.pin1, Moisture.pin2, PH.pin5
  GND: Arduino_Mini.GND, FTDI.GND, Tmp/Hmd.pin1, 10_K.Pin_1, Pantalla_LCD.Grnd, Temp/Hume5.pin7, Bateria.pin2, Celda_1.pin1, Celda_2.pin1, 100uF.-, R1.Pin_1, XBee.pin5, LUZ.pin4, Moisture.pin1, PH.pin2
  N4: Arduino_Mini.A4, LUZ.pin3
  N5: Arduino_Mini.A5, LUZ.pin2
  N6: Arduino_Mini.RAW, Bateria.pin1, D1.cathode, 100uF.+, R2.Pin_1
  N7: Arduino_Mini.A3, R2.Pin_0, R3.Pin_0
  N8: Arduino_Mini.A2, Moisture.pin3
  N9: Arduino_Mini.A1, PH.pin6
  N10: Arduino_Mini.A0, LDR.pin_1, 10_K.Pin_0
  N11: Arduino_Mini.D13/SCK, XBee.pin3
  N12: Arduino_Mini.D12/MISO, XBee.pin2
  N13: Arduino_Mini.D11_PWM/MOSI, LED1.anode
  N14: Arduino_Mini.D10_PWM/SS, Tmp/Hmd.pin3
  N15: Arduino_Mini.D7, Pantalla_LCD.SCE, Temp/Hume5.pin6
  N16: Arduino_Mini.D6_PWM, Pantalla_LCD.RST, Temp/Hume5.pin5
  N17: Arduino_Mini.D5_PWM, Pantalla_LCD.D/C
  N18: Arduino_Mini.D4, Pantalla_LCD.6_DN_(MOSI)
  N19: Arduino_Mini.D3_PWM, Pantalla_LCD.SCLK
  N20: Arduino_Mini.D2, Pantalla_LCD.LED
  N21: Celda_1.pin2, Celda_2.pin2, D1.anode
  N22: LED1.cathode, R1.Pin_0

notes:
  -n
  +r
  +
  sensor suelo A2
  xbee tx/rx 12/13
  LDR A0
  PH A1
  temp/hr pin 10
  Suelo A2
  vcc
  scl
  dat
  gnd

custom parts:
  : Nokia 5110 LCD with 8 pin. It's a 45mm*45mm module part. Description: The Nokia 5110 is a basic graphic LCD screen for lots of applications. It was originally intended for as a cell phone screen. This one is mounted on an easy to solder PCB. It uses the PCD8544 controller. The PCD8544 is a low power CMOS LCD controller/driver, designed to drive a graphic display of 48 rows and 84 columns. All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
